# Fritzing sketch wiring (saved by Fritzing 0.9.3b)

parts:
  Digispark1 = Digispark
  U1 = POT [package=pot_mammoth]
  S1 = Round Pushbutton

nets:
  N1: Digispark1.VCC, U1.E
  N2: Digispark1.GND, U1.S, S1.leg1
  N3: Digispark1.P0, S1.leg0
  N4: Digispark1.P2, U1.A

custom parts:
  Digispark: The Digispark is an Attiny85 based microcontroller development board similar to the Arduino line, only cheaper, smaller, and a bit less powerful. With a whole host of shields to extend its functionality and the ability to use the familiar Arduino IDE the Digispark is a great way to jump into electronics, or perfect for when an Arduino is too big or too much.
